# Fritzing sketch DataLogger (saved by Fritzing 0.9.2b)
breadboards: 1

parts:
  Part1 = Arduino Uno (Rev3)  # not connected
  Part3 = DeadOn RTC - DS3234 Breakout  # not connected
  Part4 = Barometric Pressure Sensor - BMP180 Breakout (GY-68)  # not connected
  U2 = microSD Socket [package=usd-socket-pp]  # not connected
  RHT1 = Humidity and Temperature Sensor RHT03  # not connected
  R1 = Resistor [tolerance=±5% resistance=220 package=THT]
  R2 = Resistor [tolerance=±5% resistance=220 package=THT]
  V1 = DC Power [voltage=5]
  D1 = Rectifier Diode [part_number=1N4001 package="300 mil [THT]"]
  R3 = Resistor [tolerance=±5% resistance=220 package=THT]
  R4 = Resistor [tolerance=±5% resistance=220 package=THT]

nets:
  N1: R1.Pin_0, R2.Pin_0
  N2: V1.V+, D1.anode
  N3: V1.V-, R4.Pin_0
  N4: D1.cathode, R3.Pin_1
  N5: R3.Pin_0, R4.Pin_1
